// Logisim project FlipFlopD.circ as structural Verilog: 1 circuit, main circuit main
module main (
  input  in_1,
  input  in_2,
  input  in_3,
  output out_4,
  output out_5
);

  wire and_1_out, and_2_out, and_3_out, and_4_out, clock_1_out, not_1_out, not_2_out, not_3_out, not_4_out,
       or_1_out, or_2_out, or_3_out, or_4_out;

  Clock clock_1 (.out(clock_1_out));
  not not_1 (not_1_out, in_2);
  and and_1 (and_1_out, out_5, in_2, not_2_out);
  not not_2 (not_2_out, clock_1_out);
  and and_2 (and_2_out, not_2_out, not_1_out, out_4);
  or or_1 (or_1_out, in_1, and_1_out, not_4_out);
  not not_3 (not_3_out, or_1_out);
  or or_2 (or_2_out, not_3_out, and_2_out, in_3);
  not not_4 (not_4_out, or_2_out);
  and and_3 (and_3_out, not_3_out, clock_1_out);
  and and_4 (and_4_out, clock_1_out, not_4_out);
  or or_3 (or_3_out, and_3_out, in_3, out_5);
  or or_4 (or_4_out, out_4, in_1, and_4_out);
  not not_5 (out_4, or_3_out);
  not not_6 (out_5, or_4_out);
endmodule
